# Fritzing sketch smart (saved by Fritzing 0.9.3b)

parts:
  LED1 = RGB LED (com. cathode, rgb) [package="5 mm [THT]"]
  부품1 = Arduino Uno (Rev3) - ICSP
  부품2 = Soil Moisture Sensor
  S1 = H-Bridge with L298N
  VCC1 = 4 x AAA Battery Mount
  M1 = DC Motor
  부품3 = LCD1602-I2C

nets:
  N1: LED1.red_anode, 부품1.D8
  GND: LED1.common_cathode, 부품1.GND, 부품2.GND, 부품3.GND
  N2: LED1.green_anode, 부품1.D9_PWM
  N3: LED1.blue_anode, 부품1.D10_PWM/SS
  N4: 부품1.A0, 부품2.SIG
  N5: 부품1.A4/SDA, 부품3.SDA
  N6: 부품1.A5/SCL, 부품3.SCL
  5V: 부품1.5V, 부품2.VCC
  N7: 부품1.D2, S1.IN1
  N8: 부품1.D3_PWM, S1.IN2
  3V3: 부품1.3V3, 부품3.VCC
  N9: S1.12V, VCC1.+
  N10: S1.GND, VCC1.-
  N11: S1.M1-01, M1.pin_2
  N12: S1.M1-02, M1.pin_1

custom parts:
  H-Bridge with L298N: h-bridge
  LCD1602-I2C: A standard character display, usually with 2x16 characters. Comes in many colors with LCM1602 IIC attached.
